// Logisim project Processor.circ as structural Verilog: 18 circuits, main circuit main
module main (
  input  in_1,
  input  in_2,
  input  [17:0] in_3,
  output [17:0] out_4
);

  wire clock_1_out, control_unit_1_alu, control_unit_1_isimmidiate, control_unit_1_jmp,
       control_unit_1_memread, control_unit_1_memwrite, control_unit_1_pcrelative, control_unit_1_pcwrite,
       control_unit_1_w, not_1_out, not_2_out;
  wire [2:0] n18bitcomparator_1_eq;
  wire [3:0] control_unit_1_rd1, control_unit_1_rd2, control_unit_1_wr, controlled_buffer_1_out;
  wire [17:0] alu_1_output, multiplexer_1_out, multiplexer_2_out, multiplexer_3_out, multiplexer_4_out,
       ram_1_data, registers_1_output1, registers_1_output2, rom_1_data, signextender6_1_out,
       signextender6_2_out, signextender10_1_out;

  Clock clock_1 (.out(clock_1_out));
  ProgramCounter programcounter_1 (
    .InputEnableBit(1'b0), .in_2(in_3), .PCWrite(control_unit_1_pcwrite), .Clock(clock_1_out),
    .ClearBit(in_2), .out(out_4), .IncrementAmount(multiplexer_1_out));
  ROM #(.addrWidth(18), .dataWidth(18)) rom_1 (.addr(out_4), .data(rom_1_data), .sel(1'b1));
  Multiplexer #(.width(18), .enable("false")) multiplexer_1 (
    .in0(18'h1), .in1(multiplexer_2_out), .out(multiplexer_1_out), .sel(control_unit_1_pcrelative));
  assign controlled_buffer_1_out = not_1_out ? control_unit_1_rd2 : 4'bz;  // Controlled_Buffer controlled_buffer_1
  SignExtender6 signextender6_1 (.in(rom_1_data[5:0]), .out(signextender6_1_out));
  not not_1 (not_1_out, control_unit_1_isimmidiate);
  registers registers_1 (
    .readRegister1(control_unit_1_rd1), .writeRegister(control_unit_1_wr),
    .readRegister2(controlled_buffer_1_out), .clockpin(clock_1_out), .Input(multiplexer_3_out),
    .W(control_unit_1_w), .Output1(registers_1_output1), .Output2(registers_1_output2));
  Control_Unit control_unit_1 (
    .wr(control_unit_1_wr), .rd1(control_unit_1_rd1), .rd2(control_unit_1_rd2), .ALU(control_unit_1_alu),
    .isImmidiate(control_unit_1_isimmidiate), .MemWrite(control_unit_1_memwrite), .W(control_unit_1_w),
    .PCWrite(control_unit_1_pcwrite), .InstructionInput(rom_1_data), .clock(clock_1_out),
    .MemRead(control_unit_1_memread), .PCRelative(control_unit_1_pcrelative), .NPZ(n18bitcomparator_1_eq),
    .JMP(control_unit_1_jmp));
  Multiplexer #(.width(18), .enable("false")) multiplexer_2 (
    .in0(signextender10_1_out), .in1(signextender6_2_out), .out(multiplexer_2_out), .sel(not_2_out));
  Multiplexer #(.width(18), .enable("false")) multiplexer_3 (
    .in0(ram_1_data), .in1(alu_1_output), .out(multiplexer_3_out), .sel(control_unit_1_alu));
  ALU alu_1 (
    .Input1(registers_1_output1), .Input2(multiplexer_4_out), .opcode(rom_1_data[17:14]),
    .Output(alu_1_output));
  Multiplexer #(.width(18), .enable("false")) multiplexer_4 (
    .in0(registers_1_output2), .in1(signextender6_1_out), .out(multiplexer_4_out),
    .sel(control_unit_1_isimmidiate));
  _18BitComparator u_18bitcomparator_1 (
    .input1(registers_1_output2), .input2(registers_1_output1), .eq(n18bitcomparator_1_eq[0]),
    .gt(n18bitcomparator_1_eq[1]), .lt(n18bitcomparator_1_eq[2]));
  not not_2 (not_2_out, control_unit_1_jmp);
  SignExtender10 signextender10_1 (.in(rom_1_data[9:0]), .out(signextender10_1_out));
  SignExtender6 signextender6_2 (.in(rom_1_data[5:0]), .out(signextender6_2_out));
  RAM #(.addrWidth(10), .dataWidth(18), .bus("separate")) ram_1 (
    .addr(rom_1_data[9:0]), .din(registers_1_output1), .data(ram_1_data), .str(control_unit_1_memwrite),
    .sel(1'b1), .clk(clock_1_out), .ld(control_unit_1_memread), .clr(in_1));

  // Notes on the sheet:
  //   contents of rom_1 (hex, n*v repeats v):
  //   14000 14440 14880 14cc0 c000 c401 2c484 8cc0 1c881 2bffd 10c02
endmodule

// CU
module Control_Unit (
  input  [2:0] NPZ,
  input  [17:0] InstructionInput,
  input  clock,
  output PCRelative,
  output MemRead,
  output MemWrite,
  output JMP,
  output W,
  output isImmidiate,
  output [3:0] wr,
  output PCWrite,
  output [3:0] rd1,
  output [3:0] rd2,
  output ALU
);

  wire and_1_out, and_2_out, and_4_out, and_5_out, and_6_out, and_7_out, and_8_out, and_9_out,
       decoder_1_out0, decoder_1_out1, decoder_1_out2, decoder_1_out3, decoder_1_out4, decoder_1_out5,
       decoder_1_out7, decoder_1_out8, decoder_1_out9, decoder_1_out10, decoder_1_out11, decoder_1_out13,
       decoder_1_out14, decoder_1_out15, decoder_1_out16, decoder_1_out17, multiplexer_1_out,
       multiplexer_2_out, not_1_out, not_2_out, not_3_out, not_4_out, not_5_out, not_6_out, or_1_out,
       or_2_out, or_3_out, or_8_out, or_9_out, PCWrite_out, register_1_q, register_2_q, register_3_q;
  wire [4:0] counter_1_q, n5adder_1_out;

  assign rd2 = or_3_out ? InstructionInput[13:10] : 4'bz;  // Controlled_Buffer controlled_buffer_1
  assign rd1 = and_1_out ? InstructionInput[13:10] : 4'bz;  // Controlled_Buffer controlled_buffer_2
  not not_1 (not_1_out, and_1_out);
  assign rd1 = not_1_out ? InstructionInput[9:6] : 4'bz;  // Controlled_Buffer controlled_buffer_3
  assign rd2 = not_2_out ? InstructionInput[5:2] : 4'bz;  // Controlled_Buffer controlled_buffer_4
  not not_2 (not_2_out, or_3_out);
  and and_1 (and_1_out, not_3_out, not_4_out, InstructionInput[16], not_5_out);
  not not_3 (not_3_out, InstructionInput[14]);
  not not_4 (not_4_out, InstructionInput[15]);
  not not_5 (not_5_out, InstructionInput[17]);
  or or_1 (or_1_out, NPZ[1], NPZ[0]);
  or or_2 (or_2_out, NPZ[2], NPZ[0]);
  _5Adder u_5adder_1 (
    .In1({1'b0, InstructionInput[17:14]}), .In2(5'b00010), .Cin(1'b0), .Out(n5adder_1_out));  // open: Cout
  or or_3 (or_3_out, decoder_1_out13, decoder_1_out14, decoder_1_out15, decoder_1_out16, decoder_1_out17);
  Counter #(.width(5), .max('h1f), .trigger("falling")) counter_1 (
    .load(decoder_1_out1), .D(n5adder_1_out), .count(decoder_1_out0), .Q(counter_1_q), .clk(clock),
    .clr(and_2_out));  // open: carry
  and and_2 (and_2_out, not_6_out, multiplexer_1_out, register_1_q);
  not not_6 (not_6_out, decoder_1_out0);
  Multiplexer #(.enable("false")) multiplexer_1 (
    .in0(1'b1), .in1(register_2_q), .out(multiplexer_1_out), .sel(decoder_1_out5));
  Register #(.width(1)) register_1 (.D(multiplexer_2_out), .en(1'b1), .Q(register_1_q), .clk(clock), .clr(1'b0));
  Decoder #(.select(5), .enable("false")) decoder_1 (
    .out0(decoder_1_out0), .out1(decoder_1_out1), .out2(decoder_1_out2), .out3(decoder_1_out3),
    .out4(decoder_1_out4), .out5(decoder_1_out5), .out6(MemWrite), .out7(decoder_1_out7),
    .out8(decoder_1_out8), .out9(decoder_1_out9), .out10(decoder_1_out10), .out11(decoder_1_out11),
    .out12(JMP), .out13(decoder_1_out13), .out14(decoder_1_out14), .out15(decoder_1_out15),
    .out16(decoder_1_out16), .out17(decoder_1_out17), .sel(counter_1_q));  // open: out18, out19, out20, out21, out22, out23, out24, out25, out26, out27, out28, out29, out30, out31
  Register #(.width(1)) register_2 (.D(register_3_q), .en(1'b1), .Q(register_2_q), .clk(clock), .clr(1'b0));
  Register #(.width(1)) register_3 (.D(decoder_1_out5), .en(1'b1), .Q(register_3_q), .clk(clock), .clr(1'b0));
  Multiplexer #(.enable("false")) multiplexer_2 (
    .in0(PCWrite), .in1(decoder_1_out5), .out(multiplexer_2_out), .sel(decoder_1_out5));
  and and_3 (MemRead, decoder_1_out5, register_3_q);
  or or_4 (ALU, decoder_1_out11, decoder_1_out10, decoder_1_out9, decoder_1_out8, decoder_1_out7, decoder_1_out4, decoder_1_out3, decoder_1_out2);
  and and_4 (and_4_out, decoder_1_out5, register_3_q);
  and and_5 (and_5_out, or_2_out, decoder_1_out17);
  or or_5 (W, MemRead, decoder_1_out2, decoder_1_out3, decoder_1_out4, decoder_1_out7, decoder_1_out8, decoder_1_out9, decoder_1_out10, decoder_1_out11);
  or or_6 (isImmidiate, decoder_1_out7, decoder_1_out8, decoder_1_out9, decoder_1_out11);
  and and_6 (and_6_out, or_1_out, decoder_1_out16);
  and and_7 (and_7_out, NPZ[2], decoder_1_out15);
  and and_8 (and_8_out, NPZ[1], decoder_1_out14);
  and and_9 (and_9_out, NPZ[0], decoder_1_out13);
  or u_PCWrite (PCWrite_out, and_4_out, MemWrite, decoder_1_out2, decoder_1_out3, decoder_1_out4, decoder_1_out7, decoder_1_out8, decoder_1_out9, decoder_1_out10, decoder_1_out11);
  or or_7 (PCRelative, and_5_out, and_6_out, and_7_out, and_8_out, and_9_out, JMP);
  or or_8 (or_8_out, decoder_1_out17, decoder_1_out16, decoder_1_out15, decoder_1_out14, decoder_1_out13);
  or or_9 (or_9_out, or_8_out, PCWrite_out);
  or or_10 (PCWrite, PCRelative, or_9_out);

  assign wr = InstructionInput[13:10];

  // Notes on the sheet:
  //   Fetch1
  //   Fetch2
  //   AND
  //   OR
  //   ADD
  //   LD
  //   ST
  //   ANDI
  //   ORI
  //   ADDI
  //   XOR
  //   XORI
  //   JUMP
  //   BEQ
  //   BGT
  //   BLT
  //   BGE
  //   BLE
endmodule

// Register
module registers (
  input  [17:0] Input,
  input  [3:0] readRegister1,
  input  [3:0] writeRegister,
  input  [3:0] readRegister2,
  input  W,
  input  clockpin,
  output [17:0] Output1,
  output [17:0] Output2
);

  wire and_1_out, and_2_out, and_3_out, and_4_out, and_5_out, and_6_out, and_7_out, and_8_out, and_9_out,
       and_10_out, and_11_out, and_12_out, and_13_out, and_14_out, and_15_out, and_16_out, decoder_1_out0,
       decoder_1_out1, decoder_1_out2, decoder_1_out3, decoder_1_out4, decoder_1_out5, decoder_1_out6,
       decoder_1_out7, decoder_1_out8, decoder_1_out9, decoder_1_out10, decoder_1_out11, decoder_1_out12,
       decoder_1_out13, decoder_1_out14, decoder_1_out15;
  wire [17:0] register_1_q, register_2_q, register_3_q, register_4_q, register_5_q, register_6_q,
       register_7_q, register_8_q, register_9_q, register_10_q, register_11_q, register_12_q, register_13_q,
       register_14_q, register_15_q, register_16_q;

  Decoder #(.select(4)) decoder_1 (
    .out0(decoder_1_out0), .out1(decoder_1_out1), .out2(decoder_1_out2), .out3(decoder_1_out3),
    .out4(decoder_1_out4), .out5(decoder_1_out5), .out6(decoder_1_out6), .out7(decoder_1_out7),
    .out8(decoder_1_out8), .out9(decoder_1_out9), .out10(decoder_1_out10), .out11(decoder_1_out11),
    .out12(decoder_1_out12), .out13(decoder_1_out13), .out14(decoder_1_out14), .out15(decoder_1_out15),
    .sel(writeRegister));  // open: en
  and and_1 (and_1_out, decoder_1_out0, W);
  and and_2 (and_2_out, decoder_1_out1, W);
  and and_3 (and_3_out, decoder_1_out2, W);
  and and_4 (and_4_out, decoder_1_out3, W);
  and and_5 (and_5_out, decoder_1_out4, W);
  and and_6 (and_6_out, decoder_1_out5, W);
  and and_7 (and_7_out, decoder_1_out6, W);
  and and_8 (and_8_out, decoder_1_out7, W);
  and and_9 (and_9_out, decoder_1_out8, W);
  and and_10 (and_10_out, decoder_1_out9, W);
  and and_11 (and_11_out, decoder_1_out10, W);
  and and_12 (and_12_out, decoder_1_out11, W);
  and and_13 (and_13_out, decoder_1_out12, W);
  and and_14 (and_14_out, decoder_1_out13, W);
  and and_15 (and_15_out, decoder_1_out14, W);
  and and_16 (and_16_out, decoder_1_out15, W);
  Register #(.width(18)) register_1 (.D(Input), .en(and_1_out), .Q(register_1_q), .clk(clockpin), .clr(1'b0));
  Register #(.width(18)) register_2 (.D(Input), .en(and_2_out), .Q(register_2_q), .clk(clockpin), .clr(1'b0));
  Register #(.width(18)) register_3 (.D(Input), .en(and_3_out), .Q(register_3_q), .clk(clockpin), .clr(1'b0));
  Register #(.width(18)) register_4 (.D(Input), .en(and_4_out), .Q(register_4_q), .clk(clockpin), .clr(1'b0));
  Register #(.width(18)) register_5 (.D(Input), .en(and_5_out), .Q(register_5_q), .clk(clockpin), .clr(1'b0));
  Register #(.width(18)) register_6 (.D(Input), .en(and_6_out), .Q(register_6_q), .clk(clockpin), .clr(1'b0));
  Register #(.width(18)) register_7 (.en(and_7_out), .Q(register_7_q), .clk(clockpin), .clr(1'b0));  // open: D
  Register #(.width(18)) register_8 (.D(Input), .en(and_8_out), .Q(register_8_q), .clk(clockpin), .clr(1'b0));
  Register #(.width(18)) register_9 (.D(Input), .en(and_9_out), .Q(register_9_q), .clk(clockpin), .clr(1'b0));
  Register #(.width(18)) register_10 (.D(Input), .en(and_10_out), .Q(register_10_q), .clk(clockpin), .clr(1'b0));
  Register #(.width(18)) register_11 (.D(Input), .en(and_11_out), .Q(register_11_q), .clk(clockpin), .clr(1'b0));
  Register #(.width(18)) register_12 (.D(Input), .en(and_12_out), .Q(register_12_q), .clk(clockpin), .clr(1'b0));
  Register #(.width(18)) register_13 (.D(Input), .en(and_13_out), .Q(register_13_q), .clk(clockpin), .clr(1'b0));
  Register #(.width(18)) register_14 (.D(Input), .en(and_14_out), .Q(register_14_q), .clk(clockpin), .clr(1'b0));
  Register #(.width(18)) register_15 (.D(Input), .en(and_15_out), .Q(register_15_q), .clk(clockpin), .clr(1'b0));
  Register #(.width(18)) register_16 (.D(Input), .en(and_16_out), .Q(register_16_q), .clk(clockpin), .clr(1'b0));
  Multiplexer #(.select(4), .width(18)) multiplexer_1 (
    .in0(register_1_q), .in1(register_2_q), .in2(register_3_q), .in3(register_4_q), .in4(register_5_q),
    .in5(register_6_q), .in6(register_7_q), .in7(register_8_q), .in8(register_9_q), .in9(register_10_q),
    .in10(register_11_q), .in11(register_12_q), .in12(register_13_q), .in13(register_14_q),
    .in14(register_15_q), .in15(register_16_q), .out(Output1), .sel(readRegister1));  // open: en
  Multiplexer #(.select(4), .width(18)) multiplexer_2 (
    .in0(register_1_q), .in1(register_2_q), .in2(register_3_q), .in3(register_4_q), .in4(register_5_q),
    .in5(register_6_q), .in6(register_7_q), .in7(register_8_q), .in8(register_9_q), .in9(register_10_q),
    .in10(register_11_q), .in11(register_12_q), .in12(register_13_q), .in13(register_14_q),
    .in14(register_15_q), .in15(register_16_q), .out(Output2), .sel(readRegister2));  // open: en
endmodule

// +1
module _1Adder (
  input  In1,
  input  In2,
  input  Cin,
  output Out,
  output Cout
);

  wire and_1_out, and_2_out, xor_1_out;

  xor xor_1 (xor_1_out, In1, In2);
  and and_1 (and_1_out, Cin, xor_1_out);
  and and_2 (and_2_out, In1, In2);
  xor xor_2 (Out, xor_1_out, Cin);
  or or_1 (Cout, and_1_out, and_2_out);
endmodule

// 2Add
module _2Adder (
  input  [1:0] In1,
  input  [1:0] In2,
  input  Cin,
  output [1:0] Out,
  output Cout
);

  wire n1adder_1_cout;

  _1Adder u_1adder_1 (.In1(In1[0]), .In2(In2[0]), .Cin(Cin), .Out(Out[0]), .Cout(n1adder_1_cout));
  _1Adder u_1adder_2 (.In1(In1[1]), .In2(In2[1]), .Cin(n1adder_1_cout), .Out(Out[1]), .Cout(Cout));
endmodule

// +3
module _3Adder (
  input  [2:0] In1,
  input  [2:0] In2,
  input  Cin,
  output [2:0] Out,
  output Cout
);

  wire n1adder_1_cout, n1adder_2_cout;

  _1Adder u_1adder_1 (.In1(In1[0]), .In2(In2[0]), .Cin(Cin), .Out(Out[0]), .Cout(n1adder_1_cout));
  _1Adder u_1adder_2 (.In1(In1[1]), .In2(In2[1]), .Cin(n1adder_1_cout), .Out(Out[1]), .Cout(n1adder_2_cout));
  _1Adder u_1adder_3 (.In1(In1[2]), .In2(In2[2]), .Cin(n1adder_2_cout), .Out(Out[2]), .Cout(Cout));
endmodule

module _5Adder (
  input  [4:0] In1,
  input  [4:0] In2,
  input  Cin,
  output [4:0] Out,
  output Cout
);

  wire n1adder_1_cout, n1adder_2_cout, n1adder_3_cout, n1adder_4_cout;

  _1Adder u_1adder_1 (.In1(In1[0]), .In2(In2[0]), .Cin(Cin), .Out(Out[0]), .Cout(n1adder_1_cout));
  _1Adder u_1adder_2 (.In1(In1[1]), .In2(In2[1]), .Cin(n1adder_1_cout), .Out(Out[1]), .Cout(n1adder_2_cout));
  _1Adder u_1adder_3 (.In1(In1[2]), .In2(In2[2]), .Cin(n1adder_2_cout), .Out(Out[2]), .Cout(n1adder_3_cout));
  _1Adder u_1adder_4 (.In1(In1[3]), .In2(In2[3]), .Cin(n1adder_3_cout), .Out(Out[3]), .Cout(n1adder_4_cout));
  _1Adder u_1adder_5 (.In1(In1[4]), .In2(In2[4]), .Cin(n1adder_4_cout), .Out(Out[4]), .Cout(Cout));
endmodule

// +9
module _9Adder (
  input  [8:0] In2,
  input  [8:0] In1,
  input  Cin,
  output [8:0] out_4,
  output Cout
);

  wire n3adder_1_cout, n3adder_2_cout;

  _3Adder u_3adder_1 (.In1(In2[2:0]), .In2(In1[2:0]), .Cin(Cin), .Out(out_4[2:0]), .Cout(n3adder_1_cout));
  _3Adder u_3adder_2 (.In1(In2[5:3]), .In2(In1[5:3]), .Cin(n3adder_1_cout), .Out(out_4[5:3]), .Cout(n3adder_2_cout));
  _3Adder u_3adder_3 (.In1(In2[8:6]), .In2(In1[8:6]), .Cin(n3adder_2_cout), .Out(out_4[8:6]), .Cout(Cout));
endmodule

// +18
module _18Adder (
  input  [17:0] In1,
  input  [17:0] In2,
  output out_3,
  output [17:0] out_4
);

  wire n9adder_1_cout;

  _9Adder u_9adder_1 (.In2(In1[8:0]), .In1(In2[8:0]), .Cin(1'b0), .out_4(out_4[8:0]), .Cout(n9adder_1_cout));
  _9Adder u_9adder_2 (.In2(In1[17:9]), .In1(In2[17:9]), .Cin(n9adder_1_cout), .out_4(out_4[17:9]), .Cout(out_3));
endmodule

module ZeroExtender10 (
  input  [9:0] Input,
  output [17:0] Output
);


  assign Output = {{8{1'b0}}, Input};
endmodule

module SignExtender14 (
  input  [13:0] in_1,
  output [17:0] out_2
);


  assign out_2 = {{5{in_1[13]}}, in_1[12:0]};
endmodule

// Ext6
module SignExtender6 (
  input  [5:0] in,
  output [17:0] out
);


  assign out = {{13{in[5]}}, in[4:0]};
endmodule

// Ext10
module SignExtender10 (
  input  [9:0] in,
  output [17:0] out
);


  assign out = {{9{in[9]}}, in[8:0]};
endmodule

// HC
module HalfComparator (
  input  a,
  input  b,
  output eq,
  output gt,
  output lt
);

  wire not_1_out, not_2_out;

  not not_1 (not_1_out, b);
  not not_2 (not_2_out, a);
  xnor xnor_1 (eq, a, b);
  and and_1 (gt, a, not_1_out);
  and and_2 (lt, not_2_out, b);
endmodule

// FC
module Full_Comparator (
  input  a,
  input  b,
  input  eq_in,
  input  gt_in,
  input  lt_in,
  output eq,
  output gt,
  output lt
);

  wire and_1_out, and_2_out, not_1_out, not_2_out, xnor_1_out;

  not not_1 (not_1_out, b);
  not not_2 (not_2_out, a);
  xnor xnor_1 (xnor_1_out, a, b);
  and and_1 (and_1_out, eq_in, a, not_1_out);
  and and_2 (and_2_out, eq_in, not_2_out, b);
  or or_1 (gt, and_1_out, gt_in);
  or or_2 (lt, and_2_out, lt_in);
  and and_3 (eq, xnor_1_out, eq_in);
endmodule

// CMP
module _18BitComparator (
  input  [17:0] input1,
  input  [17:0] input2,
  output eq,
  output gt,
  output lt
);

  wire full_comparator_1_eq, full_comparator_1_gt, full_comparator_1_lt, full_comparator_2_eq,
       full_comparator_2_gt, full_comparator_2_lt, full_comparator_3_eq, full_comparator_3_gt,
       full_comparator_3_lt, full_comparator_4_eq, full_comparator_4_gt, full_comparator_4_lt,
       full_comparator_5_eq, full_comparator_5_gt, full_comparator_5_lt, full_comparator_6_eq,
       full_comparator_6_gt, full_comparator_6_lt, full_comparator_7_eq, full_comparator_7_gt,
       full_comparator_7_lt, full_comparator_8_eq, full_comparator_8_gt, full_comparator_8_lt,
       full_comparator_9_eq, full_comparator_9_gt, full_comparator_9_lt, full_comparator_10_eq,
       full_comparator_10_gt, full_comparator_10_lt, full_comparator_11_eq, full_comparator_11_gt,
       full_comparator_11_lt, full_comparator_12_eq, full_comparator_12_gt, full_comparator_12_lt,
       full_comparator_13_eq, full_comparator_13_gt, full_comparator_13_lt, full_comparator_14_eq,
       full_comparator_14_gt, full_comparator_14_lt, full_comparator_15_eq, full_comparator_15_gt,
       full_comparator_15_lt, full_comparator_16_gt, full_comparator_16_lt, full_comparator_17_eq,
       full_comparator_17_gt, full_comparator_17_lt, halfcomparator_1_eq, halfcomparator_1_gt,
       halfcomparator_1_lt, multiplexer_1_out, multiplexer_3_out, not_1_out, not_2_out, not_3_out, not_4_out;

  HalfComparator halfcomparator_1 (
    .a(input1[17]), .b(input2[17]), .eq(halfcomparator_1_eq), .gt(halfcomparator_1_gt),
    .lt(halfcomparator_1_lt));
  Full_Comparator full_comparator_1 (
    .a(input1[16]), .b(input2[16]), .eq_in(halfcomparator_1_eq), .gt_in(halfcomparator_1_gt),
    .lt_in(halfcomparator_1_lt), .eq(full_comparator_1_eq), .gt(full_comparator_1_gt),
    .lt(full_comparator_1_lt));
  Full_Comparator full_comparator_2 (
    .a(input1[15]), .b(input2[15]), .eq_in(full_comparator_1_eq), .gt_in(full_comparator_1_gt),
    .lt_in(full_comparator_1_lt), .eq(full_comparator_2_eq), .gt(full_comparator_2_gt),
    .lt(full_comparator_2_lt));
  Full_Comparator full_comparator_3 (
    .a(input1[13]), .b(input2[13]), .eq_in(full_comparator_4_eq), .gt_in(full_comparator_4_gt),
    .lt_in(full_comparator_4_lt), .eq(full_comparator_3_eq), .gt(full_comparator_3_gt),
    .lt(full_comparator_3_lt));
  Full_Comparator full_comparator_4 (
    .a(input1[14]), .b(input2[14]), .eq_in(full_comparator_2_eq), .gt_in(full_comparator_2_gt),
    .lt_in(full_comparator_2_lt), .eq(full_comparator_4_eq), .gt(full_comparator_4_gt),
    .lt(full_comparator_4_lt));
  Full_Comparator full_comparator_5 (
    .a(input1[11]), .b(input2[11]), .eq_in(full_comparator_6_eq), .gt_in(full_comparator_6_gt),
    .lt_in(full_comparator_6_lt), .eq(full_comparator_5_eq), .gt(full_comparator_5_gt),
    .lt(full_comparator_5_lt));
  Full_Comparator full_comparator_6 (
    .a(input1[12]), .b(input2[12]), .eq_in(full_comparator_3_eq), .gt_in(full_comparator_3_gt),
    .lt_in(full_comparator_3_lt), .eq(full_comparator_6_eq), .gt(full_comparator_6_gt),
    .lt(full_comparator_6_lt));
  Full_Comparator full_comparator_7 (
    .a(input1[10]), .b(input2[10]), .eq_in(full_comparator_5_eq), .gt_in(full_comparator_5_gt),
    .lt_in(full_comparator_5_lt), .eq(full_comparator_7_eq), .gt(full_comparator_7_gt),
    .lt(full_comparator_7_lt));
  Full_Comparator full_comparator_8 (
    .a(input1[8]), .b(input2[8]), .eq_in(full_comparator_9_eq), .gt_in(full_comparator_9_gt),
    .lt_in(full_comparator_9_lt), .eq(full_comparator_8_eq), .gt(full_comparator_8_gt),
    .lt(full_comparator_8_lt));
  Full_Comparator full_comparator_9 (
    .a(input1[9]), .b(input2[9]), .eq_in(full_comparator_7_eq), .gt_in(full_comparator_7_gt),
    .lt_in(full_comparator_7_lt), .eq(full_comparator_9_eq), .gt(full_comparator_9_gt),
    .lt(full_comparator_9_lt));
  Full_Comparator full_comparator_10 (
    .a(input1[7]), .b(input2[7]), .eq_in(full_comparator_8_eq), .gt_in(full_comparator_8_gt),
    .lt_in(full_comparator_8_lt), .eq(full_comparator_10_eq), .gt(full_comparator_10_gt),
    .lt(full_comparator_10_lt));
  Full_Comparator full_comparator_11 (
    .a(input1[5]), .b(input2[5]), .eq_in(full_comparator_12_eq), .gt_in(full_comparator_12_gt),
    .lt_in(full_comparator_12_lt), .eq(full_comparator_11_eq), .gt(full_comparator_11_gt),
    .lt(full_comparator_11_lt));
  Full_Comparator full_comparator_12 (
    .a(input1[6]), .b(input2[6]), .eq_in(full_comparator_10_eq), .gt_in(full_comparator_10_gt),
    .lt_in(full_comparator_10_lt), .eq(full_comparator_12_eq), .gt(full_comparator_12_gt),
    .lt(full_comparator_12_lt));
  Full_Comparator full_comparator_13 (
    .a(input1[3]), .b(input2[3]), .eq_in(full_comparator_14_eq), .gt_in(full_comparator_14_gt),
    .lt_in(full_comparator_14_lt), .eq(full_comparator_13_eq), .gt(full_comparator_13_gt),
    .lt(full_comparator_13_lt));
  Full_Comparator full_comparator_14 (
    .a(input1[4]), .b(input2[4]), .eq_in(full_comparator_11_eq), .gt_in(full_comparator_11_gt),
    .lt_in(full_comparator_11_lt), .eq(full_comparator_14_eq), .gt(full_comparator_14_gt),
    .lt(full_comparator_14_lt));
  Full_Comparator full_comparator_15 (
    .a(input1[2]), .b(input2[2]), .eq_in(full_comparator_13_eq), .gt_in(full_comparator_13_gt),
    .lt_in(full_comparator_13_lt), .eq(full_comparator_15_eq), .gt(full_comparator_15_gt),
    .lt(full_comparator_15_lt));
  Full_Comparator full_comparator_16 (
    .a(input1[0]), .b(input2[0]), .eq_in(full_comparator_17_eq), .gt_in(full_comparator_17_gt),
    .lt_in(full_comparator_17_lt), .eq(eq), .gt(full_comparator_16_gt), .lt(full_comparator_16_lt));
  Full_Comparator full_comparator_17 (
    .a(input1[1]), .b(input2[1]), .eq_in(full_comparator_15_eq), .gt_in(full_comparator_15_gt),
    .lt_in(full_comparator_15_lt), .eq(full_comparator_17_eq), .gt(full_comparator_17_gt),
    .lt(full_comparator_17_lt));
  not not_1 (not_1_out, full_comparator_16_gt);
  not not_2 (not_2_out, full_comparator_16_lt);
  Multiplexer #(.enable("false")) multiplexer_1 (
    .in0(full_comparator_16_gt), .in1(not_1_out), .out(multiplexer_1_out), .sel(input2[17]));
  Multiplexer #(.enable("false")) multiplexer_2 (.in0(multiplexer_1_out), .in1(not_3_out), .out(gt), .sel(input1[17]));
  not not_3 (not_3_out, multiplexer_1_out);
  Multiplexer #(.enable("false")) multiplexer_3 (
    .in0(full_comparator_16_lt), .in1(not_2_out), .out(multiplexer_3_out), .sel(input2[17]));
  not not_4 (not_4_out, multiplexer_3_out);
  Multiplexer #(.enable("false")) multiplexer_4 (.in0(multiplexer_3_out), .in1(not_4_out), .out(lt), .sel(input1[17]));
endmodule

module ALU (
  input  [3:0] opcode,
  input  [17:0] Input1,
  input  [17:0] Input2,
  output [17:0] Output
);

  wire and_2_out, and_3_out, and_4_out, and_5_out, and_6_out, and_7_out, and_8_out, and_9_out,
       n18adder_1_out_3, or_2_out, or_3_out, or_4_out, or_5_out;
  wire [17:0] and_1_out, n18adder_1_out_4, or_1_out, xor_1_out;

  assign and_1_out = Input1 & Input2;  // AND_Gate and_1, 18 bits wide
  assign or_1_out = Input1 | Input2;  // OR_Gate or_1, 18 bits wide
  _18Adder u_18adder_1 (.In1(Input1), .In2(Input2), .out_3(n18adder_1_out_3), .out_4(n18adder_1_out_4));
  assign xor_1_out = Input1 ^ Input2;  // XOR_Gate xor_1, 18 bits wide
  and and_2 (and_2_out, ~opcode[3], ~opcode[2], ~opcode[1], ~opcode[0]);  // AND_Gate
  and and_3 (and_3_out, ~opcode[3], opcode[2], ~opcode[1], opcode[0]);  // AND_Gate
  or or_2 (or_2_out, and_2_out, and_3_out);
  assign Output = or_2_out ? and_1_out : 18'bz;  // Controlled_Buffer controlled_buffer_1
  and and_4 (and_4_out, ~opcode[3], ~opcode[2], ~opcode[1], opcode[0]);  // AND_Gate
  and and_5 (and_5_out, ~opcode[3], opcode[2], opcode[1], ~opcode[0]);  // AND_Gate
  or or_3 (or_3_out, and_4_out, and_5_out);
  assign Output = or_3_out ? or_1_out : 18'bz;  // Controlled_Buffer controlled_buffer_2
  and and_6 (and_6_out, ~opcode[3], ~opcode[2], opcode[1], ~opcode[0]);  // AND_Gate
  and and_7 (and_7_out, ~opcode[3], opcode[2], opcode[1], opcode[0]);  // AND_Gate
  or or_4 (or_4_out, and_6_out, and_7_out);
  assign Output = or_4_out ? n18adder_1_out_4 : 18'bz;  // Controlled_Buffer controlled_buffer_3
  and and_8 (and_8_out, opcode[3], ~opcode[2], ~opcode[1], ~opcode[0]);  // AND_Gate
  and and_9 (and_9_out, opcode[3], ~opcode[2], ~opcode[1], opcode[0]);  // AND_Gate
  or or_5 (or_5_out, and_8_out, and_9_out);
  assign Output = or_5_out ? xor_1_out : 18'bz;  // Controlled_Buffer controlled_buffer_4
  // also tied to GND on the sheet: n18adder_1_out_3
endmodule

// PC
module ProgramCounter (
  input  InputEnableBit,
  input  [17:0] in_2,
  input  [17:0] IncrementAmount,
  input  PCWrite,
  input  Clock,
  input  ClearBit,
  output [17:0] out
);

  wire not_1_out;
  wire [17:0] controlled_buffer_1_out, n18adder_1_out_4;

  not not_1 (not_1_out, InputEnableBit);
  assign controlled_buffer_1_out = not_1_out ? n18adder_1_out_4 : 18'bz;  // Controlled_Buffer controlled_buffer_1
  assign controlled_buffer_1_out = InputEnableBit ? in_2 : 18'bz;  // Controlled_Buffer controlled_buffer_2
  Register #(.width(18)) register_1 (.D(controlled_buffer_1_out), .en(PCWrite), .Q(out), .clk(Clock), .clr(ClearBit));
  _18Adder u_18adder_1 (.In1(out), .In2(IncrementAmount), .out_4(n18adder_1_out_4));  // open: out_3
endmodule
